// Logisim project CPU_8bits.circ as structural Verilog: 3 circuits, main circuit main
module main (
);

  wire undriven;
  wire [3:0] undriven_2;
  wire [7:0] alu_8bit_xmx077_1_out_4, AR1_out_5, controlled_buffer_1_out, controlled_buffer_3_out, DR1_out_5,
       DR2_out_5, ER_out_5, ext_1_out_2, main_1_a_out, main_1_b_out;

  DR DR2 (.in_1(main_1_a_out), .out_5(DR2_out_5));  // open: LDDR, CLK, CLEAR
  ALU_8bit_xmx077 alu_8bit_xmx077_1 (
    .A(DR2_out_5), .B(DR1_out_5), .out_4(alu_8bit_xmx077_1_out_4));  // open: in_3, out_5, out_6, out_7
  RF_4_main main_1 (
    .D_in(ER_out_5), .A_out(main_1_a_out), .B_out(main_1_b_out));  // open: clk, RS, RD, reset, Write, WRD, R1_o, R0_o, R3_o, R2_o
  DR ER (.in_1(controlled_buffer_1_out), .out_5(ER_out_5));  // open: LDDR, CLK, CLEAR
  Controlled_Buffer #(.width(8)) controlled_buffer_1 (
    .in(alu_8bit_xmx077_1_out_4), .out(controlled_buffer_1_out));  // open: en
  DR DR1 (.in_1(main_1_b_out), .out_5(DR1_out_5));  // open: LDDR, CLK, CLEAR
  Controlled_Buffer #(.width(8)) controlled_buffer_2 (.in(main_1_b_out), .out(controlled_buffer_1_out));  // open: en
  RAM_8bits_main main_2 (
    .Add_in(AR1_out_5), .D_in(controlled_buffer_3_out), .D_out(controlled_buffer_1_out), .CLR(undriven));  // open: Write, cs, clk, Read
  Controlled_Buffer #(.width(8)) controlled_buffer_3 (
    .in(controlled_buffer_1_out), .out(controlled_buffer_3_out));  // open: en
  DR AR1 (.in_1(controlled_buffer_1_out), .out_5(AR1_out_5), .CLEAR(undriven));  // open: LDDR, CLK
  Multiplexer #(.width(8), .enable("false")) multiplexer_1 (
    .in0(controlled_buffer_1_out), .in1(ext_1_out_2));  // open: out, sel
  EXT ext_1 (.in_1(undriven_2), .out_2(ext_1_out_2));
endmodule

module DR (
  input  [7:0] in_1,
  input  LDDR,
  input  CLK,
  input  CLEAR,
  output [7:0] out_5
);

  Register register_1 (.D(in_1), .en(LDDR), .Q(out_5), .clk(CLK), .clr(CLEAR));
endmodule

module EXT (
  input  [3:0] in_1,
  output [7:0] out_2
);


  assign out_2 = {4'b0000, in_1};
endmodule
